// Digital circuit UC.dig as structural Verilog
module UC (
  input  [31:0] E,
  output WREG,
  output [2:0] ULAop,
  output CI,
  output [1:0] REG,
  output WM,
  output [1:0] IMMop,
  output IS,
  output H,
  output jalr,
  output J,
  output B
);

  wire I, R;

  or or_1 (WREG, J, I, R);
  or or_2 (CI, WM, I);
  or or_3 (REG[1], J, jalr);
  unidade unidade_1 (
    .opc(E[6:0]), .f3(E[14:12]), .f7(E[31:25]), .J(J), .R(R), .S(WM), .I(I), .B(B), .LW(REG[0]), .jalr(jalr),
    .IS(IS), .imm_op(IMMop), .ula_op(ULAop), .H(H));

  // Other names for the same wires on the sheet: imm_op[1:0] = IMMop; lw = REG[0]; S = WM; ula_op[2:0] = ULAop
endmodule
