// Digital circuit projeto.dig as structural Verilog
module projeto (
  input  clock
);

  wire and_1_out, and_2_out, B, CI, comparator_1_eq, H, IS, J, jalr, multiplexer_2_out, WM, WREG, zero;
  wire [0:0] pc_src;
  wire [1:0] IMMop, REG;
  wire [2:0] ULAop;
  wire [31:0] add_2_s, calc_imm_1_imm, MI_d, multiplexer_1_out, multiplexer_3_out, multiplexer_4_out,
       not_1_out, opA, opB, pc_plus_4, PC_q, ramdualport_1_d, ula_1_r, ULAout;

  Multiplexer #(.Selector_Bits(2), .Bits(32)) multiplexer_1 (
    .sel({jalr, pc_src[0]}), .in_0(pc_plus_4), .in_1(add_2_s), .in_2(ULAout), .in_3(ULAout),
    .out(multiplexer_1_out));
  // Probe on multiplexer_1_out
  Register #(.Bits(32), .isProgramCounter("true")) PC (.D(multiplexer_1_out), .C(clock), .en(H), .Q(PC_q));
  // Probe on PC_q
  ROM #(.AddrBits(24), .Bits(32)) MI (.A(PC_q[23:0]), .sel(1'b1), .D(MI_d));
  Add #(.Bits(32)) add_1 (.a(PC_q), .b(32'h4), .c_i(1'b0), .s(pc_plus_4));  // open: c_o
  UC uc_1 (
    .E(MI_d), .WREG(WREG), .ULAop(ULAop), .CI(CI), .REG(REG), .WM(WM), .IMMop(IMMop), .IS(IS), .H(H),
    .jalr(jalr), .J(J), .B(B));
  Comparator #(.Bits(5)) comparator_1 (.a({5{1'b0}}), .b(MI_d[11:7]), .eq(comparator_1_eq));  // open: gt, lt
  Multiplexer multiplexer_2 (.sel(comparator_1_eq), .in_0(WREG), .in_1(1'b0), .out(multiplexer_2_out));
  calc_imm calc_imm_1 (.IMMop(IMMop), .E(MI_d), .imm(calc_imm_1_imm));
  RegisterFile #(.AddrBits(5), .Bits(32)) registerfile_1 (
    .Din(multiplexer_4_out), .we(multiplexer_2_out), .Rw(MI_d[11:7]), .C(clock), .Ra(MI_d[19:15]),
    .Rb(MI_d[24:20]), .Da(opA), .Db(opB));
  Add #(.Bits(32)) add_2 (.a(PC_q), .b(calc_imm_1_imm), .c_i(1'b0), .s(add_2_s));  // open: c_o
  and and_1 (and_1_out, ~zero, ~IS, B);  // And
  and and_2 (and_2_out, zero, IS);
  Multiplexer #(.Bits(32)) multiplexer_3 (.sel(CI), .in_0(opB), .in_1(calc_imm_1_imm), .out(multiplexer_3_out));
  or or_1 (pc_src[0], and_1_out, and_2_out, J);
  ula ula_1 (.A(opA), .B(multiplexer_3_out), .ula_op(ULAop), .R(ula_1_r), .Z(zero));
  Multiplexer #(.Selector_Bits(2), .Bits(32)) multiplexer_4 (
    .sel(REG), .in_0(ULAout), .in_1(ramdualport_1_d), .in_2(pc_plus_4), .in_3(pc_plus_4),
    .out(multiplexer_4_out));
  assign not_1_out = ~ula_1_r;  // Not not_1, 32 bits wide
  Multiplexer #(.Bits(32)) multiplexer_5 (.sel(IS), .in_0(ula_1_r), .in_1(not_1_out), .out(ULAout));
  // Probe on ULAout
  RAMDualPort #(.AddrBits(24), .Bits(32)) ramdualport_1 (
    .A(ULAout[23:0]), .Din(opB), .str(WM), .C(clock), .ld(1'b1), .D(ramdualport_1_d));

  // Other names for the same wires on the sheet: pc_src[1] = jalr

  // Notes on the sheet:
  //   clock: Hz: 50000
  //   contents of MI (hex, n*v repeats v):
  //   513,0,0,0,1400593,0,0,0,100613,0,0,0,100693,0,0,0,8000ef,0,0,0
  //   ,8000000,0,0,0,c00333,0,0,0,d003b3,0,0,0,602023,0,0,0,702223,0,0,0
  //   ,200293,0,0,0,2b2da63,0,0,0,fff28e13,0,0,0,2e1e13,0,0,0,ae0e33
  //   ,0,0,0,e2e83,0,0,0,ffe28f13,0,0,0,2f1f13,0,0,0,af0f33,0,0,0,f2f83
  //   ,0,0,0,1fe8eb3,0,0,0,1de2223,0,0,0,128293,0,0,0,fd1ff06f,0,0,0,8067
endmodule
